# Fritzing sketch hidden_device (saved by Fritzing 1.0.0rc)
breadboards: 1

parts:
  part = Arduino Uno Mini LE
  FSR = Basic Force Sensing Resistor (FSR) [package=THT]
  part_2 = Resistor [tolerance=±5% power=0.25W resistance=10k part_number=. package=THT]
  part_3 = ESP8266 ESP-01 Upgraded WiFi Module [part_number=.]
  part_4 = Resistor [tolerance=±5% power=0.25W resistance=10k package=THT]
  part_5 = Resistor [tolerance=±5% power=0.25W resistance=10k package=THT]
  part_6 = Resistor [tolerance=±5% power=0.25W resistance=10k package=THT]
  Buzzer = Piezo Speaker
  part_7 = Resistor [tolerance=±5% power=0.25W resistance=220 package=THT]
  part_8 = KY-019 5V Relay Module [package="Breakout board"]
  part_9 = Battery block 9V
  part_10 = DFRobot SEN0030 [package=THT]

nets:
  N1: part.A0, FSR.pin_1, part_2.Pin_0
  N2: part.D9_PWM, part_8.S
  N3: part.D11_PWM/MOSI, part_10.P1_1
  N4: part.D13/SCK, part_7.Pin_0
  GND: part.GND, part_2.Pin_1, part_3.GND, part_4.Pin_0, Buzzer.pin1, part_8.-, part_10.P1_3
  N5: part.D3_PWM, part_3.TXD
  N6: part.D5_PWM, part_6.Pin_1
  N7: part.D7, part.RESET
  3V3: part.3V3, FSR.pin_2, part_3.VCC, part_3.CH_PD, part_8.+, part_10.P1_2
  N8: part_3.RXD, part_5.Pin_1, part_6.Pin_0
  N9: part_4.Pin_1, part_5.Pin_0
  N10: Buzzer.pin2, part_7.Pin_1
  N11: part_8.Common, part_9.+

custom parts:
  Arduino Uno Mini LE: The UNO Mini Limited Edition (LE) is a miniature version of the classic Arduino UNO board. It is based on the ATmega328P microcontroller, has USB-C connector for programming and powering the board, and pins available for connecting external power sources. It also comes with the standard set of female pin connectors, built-in LED, reset button and everything else that the standard UNO have, but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
  ESP8266 ESP-01 Upgraded WiFi Module: Upgraded Version ESP-01,all Flash are upgraded to 1M byte.Also support Cloud service remote transmission.
  KY-019 5V Relay Module: KY-019 5V Relay module, used to control AC circuits. (Special thanks to vanepp for fixing the PCB holes and other errors)
  DFRobot SEN0030: DFRobot Capacitive Touch Sensor SKU DFR0030
